# Fritzing sketch ALU (saved by Fritzing 0.9.6b)
breadboards: 6

parts:
  U1 = 74HC245 [package="DIP (Dual Inline) [THT]"]
  U2 = 74HC574 [package="DIP (Dual Inline) [THT]"]
  U3 = AS6C6264 [package="DIP (Dual Inline) [THT]"]
  U4 = AS6C6264 [package="DIP (Dual Inline) [THT]"]
  U5 = AS6C6264 [package="DIP (Dual Inline) [THT]"]
  U6 = 74HC574 [package="DIP (Dual Inline) [THT]"]
  U7 = 74HC00 [package="DIP (Dual Inline) [THT]"]
  U8 = 74HC573 [package="DIP (Dual Inline) [THT]"]
  U9 = 74HC245 [package="DIP (Dual Inline) [THT]"]
  U10 = 74HC574 [package="DIP (Dual Inline) [THT]"]
  U11 = 74HC574 [package="DIP (Dual Inline) [THT]"]

nets:
  N1: U1.A1, U1.A4
  N2: U1.A2, U3.DQ2
  N3: U1.A3, U4.DQ2
  N4: U1.A5, U1.A8
  N5: U1.A6, U2.D5
  GND: U1.GND, U2./OE, U2.GND, U6./OE, U6.GND, U7.GND
  N6: U2.D0, U2.D3
  N7: U2.D1, U3.DQ1
  N8: U2.D2, U4.DQ1
  N9: U2.D4, U2.D7
  N10: U2.D6, U5.DQ1
  N11: U3.A7, U3.A0
  N12: U3.A4, U10.Q3
  N13: U3.A3, U4.A4
  N14: U3.DQ0, U3.DQ3
  VSS: U3.Vss, U4.Vss, U5.Vss
  N15: U3.DQ4, U3.DQ7
  N16: U3.DQ6, U6.D5
  N17: U3./CE, U3.A8, U4./CE, U5./CE, U5./OE
  N18: U3./OE, U5.DQ4, U7.2A, U7.2B
  VCC: U3.Vcc, U4.A8, U4.Vcc, U5.Vcc
  N19: U4.A7, U4.A0
  N20: U4.A3, U11.Q3
  N21: U4.DQ0, U4.DQ3
  N22: U4.DQ4, U4.DQ7
  N23: U4.DQ6, U6.D6
  N24: U4./OE, U7.2Y
  N25: U5.A7, U5.A0
  N26: U5.A4, U9.B5
  N27: U5.A3, U8.Q4
  N28: U5.DQ0, U5.DQ3
  N29: U5.A8, U6.Q7
  N30: U6.D4, U6.D7
  N31: U8.Q7, U8.Q0
  N32: U9.B8, U9.B1
  N33: U10.Q7, U10.Q0
  N34: U11.Q7, U11.Q0

notes:
  Move the top chip(s) up and the bottom 574 down
  Add a 153 and a 7432; think about the positioning.
  The 7432 is for both phi1 and phi2 control lines
  Need to OR them and route through the last 7432 to clock F.
  Need to confirm the Z flag logic.
  Need to design something for writes
  Magenta wire is the carry ... still unsure about the logic

custom parts:
  74HC245: 8-bit bidrectional transceiver with straight-across pinout
  74HC574: 8-bit clocked D-type register with straight-across pinout
  AS6C6264: 8k x 8 bit CMOS static RAM
  74HC00: Quad NAND. The original 74xx part.
  74HC573: 8-bit transparent register with straight-across pinout
