# Fritzing sketch Chiptester (saved by Fritzing 0.9.6b)
breadboards: 2

parts:
  Part1 = Arduino Nano (Rev3.0)
  U1 = 74HC138 [package="DIP (Dual Inline) [THT]"]
  U2 = 74HC138 [package="DIP (Dual Inline) [THT]"]
  U3 = 74HC574 [package="DIP (Dual Inline) [THT]"]
  U4 = 74HC574 [package="DIP (Dual Inline) [THT]"]
  U5 = 74HC574 [package="DIP (Dual Inline) [THT]"]
  U6 = 74HC574 [package="DIP (Dual Inline) [THT]"]
  U7 = 74HC574 [package="DIP (Dual Inline) [THT]"]
  U8 = 74HC574 [package="DIP (Dual Inline) [THT]"]
  U9 = 74HC245 [package="DIP (Dual Inline) [THT]"]

nets:
  GND: Part1.GND, U1./E1, U1./E2, U1.GND, U2./E1, U2./E2, U2.GND, U8./OE, U8.GND, U9.GND
  VCC: Part1.D5, Part1.D12/MISO, Part1.5V, U1.Vcc, U2.Vcc, U8.Q7, U8.Q0, U8.Vcc, U9.DIR, U9.Vcc
  N1: Part1.D9, U3.Q4
  N2: Part1.A4, U2.E3
  N3: Part1.A3, U1.E3
  N4: Part1.A2, Part1.A0
  N5: Part1.A1, U1.A1
  N6: U1.A0, U1.A2
  N7: U1./Y5, U9./DIR
  N8: U1./Y4, U7.CLK
  N9: U1./Y3, U6.CLK
  N10: U1./Y2, U5.CLK
  N11: U1./Y1, U4.CLK
  N12: U1./Y0, U3./OE
  N13: U2.A0, U2.A2
  N14: U2./Y7, U8.CLK
  N15: U2./Y6, U2./Y3
  N16: U2./Y2, U2./Y0
  N17: U3.D0, U3.D7
  N18: U3.D4, U7.Q3
  N19: U3.CLK, U3.Vcc, U4./OE, U5./OE, U6./OE
  N20: U3.Q7, U3.Q0
  N21: U3.Q3, U4.D3
  N22: U4.D0, U4.D7
  N23: U4.D4, U5.D3
  GND_2: U4.GND, U5.GND, U6.GND, U7.GND
  VCC_2: U4.Q7, U4.Q0, U4.Vcc, U5.Q7, U5.Q0, U5.Vcc, U6.Q7, U6.Vcc, U7.Q7, U7.Q0, U7.Vcc
  N24: U5.D0, U5.D7
  N25: U5.D4, U6.D3
  N26: U6.D0, U6.D7
  N27: U6.D4, U7.D3
  N28: U7.D0, U7.D7
  N29: U7.D4, U8.D4
  N30: U8.D0, U8.D7
  N31: U8.D3, U9.B4
  N32: U8.Q3, U9.A1, U9.A5, U9.A7, U9.A8
  N33: U9.B8, U9.B1

notes:
  Signals at top exit to Downloader Extension. Green line exits at left to memory, terminates in rows 1-6 of west-most memory breadboard.
  574s at left originate (from top to bottom) the low address bus, high address, low data, and high data.
  The southmost 574 facing inbound is the bus interface register. The MCR is the 574 and 245 at upper right and the two pulse output decoders are adjacent to the Nano.

custom parts:
  74HC138: 3 line to 8 line decoder
  74HC574: 8-bit clocked D-type register with straight-across pinout
  74HC245: 8-bit bidrectional transceiver with straight-across pinout
