# Fritzing sketch Clock2 (saved by Fritzing 0.9.6b)
breadboards: 2

parts:
  R1 = Resistor [tolerance=±5% power=0.25 resistance=220 package=THT]
  R2 = Photocell (LDR) [package=THT]
  U1 = 74HC14 [package="DIP (Dual Inline) [THT]"]
  X1 = XTAL [package="DIP (Dual Inline) [THT]"]
  U2 = 74HC74 [package="DIP (Dual Inline) [THT]"]
  U7 = 74HC32 [package="DIP (Dual Inline) [THT]"]
  U4 = 74HC244 [package="DIP (Dual Inline) [THT]"]
  U8 = 74HC08 [package="DIP (Dual Inline) [THT]"]
  D1 = LED_BARGRAPH_10 [package=led_bargaph_10]
  R3 = Resistor [tolerance=±5% power=0.25 resistance=220 package=THT]
  R4 = Resistor [tolerance=±5% power=0.25 resistance=220 package=THT]
  U11 = 74HC574 [package="DIP (Dual Inline) [THT]"]
  R6 = Resistor [tolerance=±5% power=0.25 resistance=220 package=THT]
  R7 = Resistor [tolerance=±5% power=0.25 resistance=220 package=THT]
  D2 = LED_BARGRAPH_10 [package=led_bargaph_10]
  R8 = Resistor [tolerance=±5% power=0.25 resistance=220 package=THT]
  R9 = Resistor [tolerance=±5% power=0.25 resistance=220 package=THT]
  R10 = Resistor [tolerance=±5% power=0.25 resistance=220 package=THT]
  R11 = Resistor [tolerance=±5% power=0.25 resistance=220 package=THT]
  D3 = LED_BARGRAPH_10 [package=led_bargaph_10]
  R12 = Resistor [tolerance=±5% power=0.25 resistance=220 package=THT]
  R13 = Resistor [tolerance=±5% power=0.25 resistance=220 package=THT]
  R14 = Resistor [tolerance=±5% power=0.25 resistance=220 package=THT]
  R15 = Resistor [tolerance=±5% power=0.25 resistance=220 package=THT]
  U12 = 74HC244 [package="DIP (Dual Inline) [THT]"]

nets:
  VCC: R1.Pin_0, U1.Vcc, X1.Vcc, U2./CLR2, U2.Vcc, U7.Vcc, U4.Vcc, U8.Vcc, U12.Vcc
  N1: R1.Pin_1, R2.pin_0, U1.A4
  GND: R2.pin_1, U1.GND, X1.GND, U2.GND, U7.GND, U4./1OE, U4.GND, U8.1A, U8.1B, U8.2A, U8.2B, U8.GND, U12./1OE, U12.GND
  N2: U1.A1, U2.Q1, U12.1A2, U12.1A3, U12.2A0, U12.2A1
  N3: U1.Y1, U12.1A0, U12.1A1, U12.2A2, U12.2A3
  N4: U1.A2, U1.A3, U1.Y4, U1.A5, U1.A6
  N5: U1.Y2, U2./SET1, D1.J_C
  N6: U1.Y6, U2./SET2, U4./2OE, U8.4A, U8.4B, U12./2OE
  N7: X1.OUT, U2.CLK2, U7.3B
  N8: U2./CLR1, U11.Vcc
  N9: U2.D1, U2./Q1
  N10: U2.CLK1, U7.4B, U4.2Y0
  N11: U2.Q2, U7.3A
  N12: U2.D2, U7.1A, U7.2A, D1.I_C
  N13: U7.1B, D2.J_C, U12.2Y0
  N14: U7.2B, D2.I_C, U12./2Y2
  N15: U7.2Y, U7.4A
  N16: U7.3Y, U8.3B
  N17: U4.1A0, U4.1A1, U4.1A2, U4.1A3, U4.2A0, U4.2A1, U4.2A2, U4.2A3, U8.3Y
  N18: D1.H_A, R3.Pin_1
  N19: D1.I_A, R4.Pin_1
  N20: D1.J_A, R7.Pin_1
  N21: D1.H_C, D1.A_C
  N22: D1.E_C, U11.Q3
  N23: R3.Pin_0, R4.Pin_0, R6.Pin_0, R7.Pin_0
  N24: U11./OE, U11.GND, R6.Pin_1, R8.Pin_1, R12.Pin_1
  N25: U11.D0, U11.D7
  N26: U11.Q7, U11.Q0
  N27: D2.H_A, R9.Pin_1
  N28: D2.I_A, R10.Pin_1
  N29: D2.J_A, R11.Pin_1
  N30: D2.H_C, D2.A_C
  N31: R8.Pin_0, R9.Pin_0, R10.Pin_0, R11.Pin_0
  N32: D3.H_A, R15.Pin_1
  N33: D3.I_A, R14.Pin_1
  N34: D3.J_A, R13.Pin_1
  N35: D3.H_C, D3.A_C
  N36: R12.Pin_0, R13.Pin_0, R14.Pin_0, R15.Pin_0

custom parts:
  74HC14: Hex Schmidt-trigger inverter
  XTAL: CTS MXO45 1Mhz CMOS clock
  74HC74: Dual edge-triggered D flipflops with asynchrounous set and clear
  74HC32: Quad 2-input OR gate
  74HC244: 3-state buffer driver with split enables
  74HC08: Quad positive AND gate
  74HC574: 8-bit clocked D-type register with straight-across pinout
