# Fritzing sketch Clock3 (saved by Fritzing 0.9.6b)
breadboards: 2

parts:
  R1 = Resistor [tolerance=±5% power=0.25 resistance=220 package=THT]
  R2 = Photocell (LDR) [package=THT]
  U12 = 74HC14 [package="DIP (Dual Inline) [THT]"]
  X1 = XTAL [package="DIP (Dual Inline) [THT]"]
  U10 = 74HC74 [package="DIP (Dual Inline) [THT]"]
  U13 = 74HC32 [package="DIP (Dual Inline) [THT]"]
  U17 = 74HC244 [package="DIP (Dual Inline) [THT]"]
  U15 = 74HC08 [package="DIP (Dual Inline) [THT]"]
  U19 = LED_BARGRAPH_10 [package=led_bargaph_10]
  R3 = Resistor [tolerance=±5% power=0.25 resistance=220 package=THT]
  R4 = Resistor [tolerance=±5% power=0.25 resistance=220 package=THT]
  U11 = 74HC574 [package="DIP (Dual Inline) [THT]"]
  R6 = Resistor [tolerance=±5% power=0.25 resistance=220 package=THT]
  R7 = Resistor [tolerance=±5% power=0.25 resistance=220 package=THT]
  U20 = 74HC138 [package="DIP (Dual Inline) [THT]"]
  R8 = Resistor [tolerance=±5% power=0.25 resistance=220 package=THT]
  U21 = DIP - 16 pins [chip_label=100ohm package="DIP (Dual Inline) [THT]"]

nets:
  VCC: R1.Pin_0, U12.Vcc, X1.Vcc, U10./CLR2, U10.Vcc, U13.4A, U13.4B, U13.Vcc, U17.Vcc, U15.Vcc
  N1: R1.Pin_1, R2.pin_0, U12.A4
  GND: R2.pin_1, U12.GND, X1.GND, U10.GND, U13.GND, U17./1OE, U17.GND, U15.GND
  N2: U12.A1, U12.A2, U12.A3, U12.Y4, U12.A5, U12.A6
  N3: U12.Y2, U19.J_C
  N4: U12.Y6, U10./SET2
  N5: X1.OUT, U10.CLK2, U13.3B
  N6: U10.D1, U10./SET1, U11.Vcc
  N7: U10.CLK1, U13.1Y
  N8: U10.Q2, U13.3A
  N9: U10.D2, U19.I_C
  N10: U13.1A, U13.2A, R8.Pin_1
  N11: U13.1B, U20./Y0
  N12: U13.3Y, U15.3B
  N13: U17.1A0, U17.1A1, U17.1A2, U17.1A3, U17.2A0, U17.2A1, U17.2A2, U17.2A3, U15.3Y
  N14: U17.2Y3, U21.pin8
  N15: U17./2Y2, U21.pin7
  N16: U17.2Y1, U21.pin6
  N17: U17.2Y0, R8.Pin_0
  N18: U17.1Y3, U21.pin15
  N19: U17.1Y2, U21.pin14
  N20: U17.1Y1, U21.pin13
  N21: U17.1Y0, U21.pin12
  N22: U17./2OE, U15.4A, U15.4B
  N23: U15.1Y, U15.2A
  N24: U15.2B, U20./E2
  N25: U15.2Y, U20.E3
  N26: U19.H_A, R3.Pin_1
  N27: U19.I_A, R4.Pin_1
  N28: U19.J_A, R7.Pin_1
  N29: U19.H_C, U19.A_C
  N30: U19.E_C, U11.Q3
  N31: R3.Pin_0, R4.Pin_0, R6.Pin_0, R7.Pin_0
  N32: U11./OE, U11.GND, R6.Pin_1
  N33: U11.D0, U11.D7
  N34: U11.Q7, U11.Q0
  N35: U21.pin2, U21.pin5
  N36: U21.pin9, U21.pin11

notes:
  Wire-wrap bundles to downloader
  Power-on reset to MCR
  Three resistively-buffered clocks to north
  Power-on reset to north
  Wire-wrap bundle to memory
  Four clocks actually to west
  Unused I/O decode outputs

custom parts:
  74HC14: Hex Schmidt-trigger inverter
  XTAL: CTS MXO45 1Mhz CMOS clock
  74HC74: Dual edge-triggered D flipflops with asynchrounous set and clear
  74HC32: Quad 2-input OR gate
  74HC244: 3-state buffer driver with split enables
  74HC08: Quad positive AND gate
  74HC574: 8-bit clocked D-type register with straight-across pinout
  74HC138: 3 line to 8 line decoder
  DIP - 16 pins: A DIP stand-in part for whatever IC you want. With 16 pins on a 300mil dual inline package (DIP) footprint.
