# Fritzing sketch D-P-mem-2 (saved by Fritzing 0.9.6b)
breadboards: 2

parts:
  U1 = 74HC245 [package="DIP (Dual Inline) [THT]"]
  U2 = 74HC245 [package="DIP (Dual Inline) [THT]"]
  U3 = 74HC574 [package="DIP (Dual Inline) [THT]"]
  U4 = 74HC245 [package="DIP (Dual Inline) [THT]"]
  U5 = 74HC574 [package="DIP (Dual Inline) [THT]"]
  U6 = 74HC245 [package="DIP (Dual Inline) [THT]"]
  U7 = AS6C6264 [package="DIP (Dual Inline) [THT]"]
  U8 = 74HC32 [package="DIP (Dual Inline) [THT]"]
  U9 = 74HC00 [package="DIP (Dual Inline) [THT]"]
  U10 = 74HC32 [package="DIP (Dual Inline) [THT]"]

nets:
  GND: U1.DIR, U1.GND, U2.DIR, U2.GND
  N1: U1.A1, U1.A8
  N2: U1.B8, U1.B1
  N3: U1.B4, U6.A5
  GND_2: U1./DIR, U2./DIR, U8.GND, U9.1A, U9.1B, U9.GND, U10.GND
  VCC: U1.Vcc, U2.Vcc, U3.Vcc, U4.Vcc, U5.Vcc, U6.Vcc, U7.Vss
  N4: U2.A1, U2.A8
  N5: U2.B8, U2.B1
  N6: U2.B5, U4.A5
  GND_3: U3./OE, U3.GND, U4.GND, U5./OE, U5.GND, U6.GND
  N7: U3.D0, U3.D7
  N8: U3.D4, U4.A4
  N9: U3.CLK, U5.CLK, U8.3Y
  N10: U3.Q7, U3.Q0
  N11: U3.Q4, U7.A4
  N12: U4.DIR, U8.2A, U9.2Y
  N13: U4.A1, U4.A8
  N14: U4.B8, U4.B1
  N15: U4.B6, U7.DQ5
  N16: U4.B2, U7.DQ1
  N17: U4./DIR, U8.4Y
  N18: U5.D0, U5.D7
  N19: U5.D4, U6.A4
  N20: U5.Q4, U5.Q0
  N21: U5.Q2, U7.A11
  VCC_2: U6.DIR, U8.Vcc, U9.Vcc
  N22: U6.A1, U6.A8
  N23: U6.B5, U8.1B, U9.2A, U9.2B
  N24: U6./DIR, U7./CE
  N25: U7.A7, U7.A0
  N26: U7.DQ0, U7.DQ2
  N27: U7.DQ3, U7.DQ7
  N28: U7.A10, U7.A8
  N29: U7./OE, U10.1Y
  VCC_3: U7.CE2, U7.Vcc, U10.3A, U10.3B, U10.4A, U10.4B, U10.Vcc
  N30: U7./WE, U10.2Y
  N31: U8.1A, U8.2B, U8.4B, U9.3Y
  N32: U8.1Y, U10.2A
  N33: U8.2Y, U10.1B
  N34: U8.3B, U8.4A, U10.1A, U10.2B
  N35: U9.3A, U9.3B, U9.4Y

notes:
  Control signals - see also the Google drawing:
  Display driver 245s: both DIR:1 and /OE strapped low.
  Op-cycle 15:8 transceiver: DIR:1 strapped inbound (high). /OE = CTL/OP
  Ctl-cycle 15:8 register: CLK = OP/CTL | SYSCLK. /OE strapped low.
  Op-cycle 7:0 transceiver: DIR:1 = ! SYSBUS:12. /OE = CLK-OP-PD#
  Ctl-cycle 7:0 register CLK = OP/CTL | SYSCLK. /OE strapped low.
  RAM /WE: SYSCLK | (OP-PD# | SYSBUS:12)
  RAM /OE: SYSCLK | (OP-PD# | ! SYSBUS:12)
  RAM /CE: OP-PD# (Or does this come to late for a chip enable? Could use CTL/OP.)
  RAM CE2: Strapped high.

custom parts:
  74HC245: 8-bit bidrectional transceiver with straight-across pinout
  74HC574: 8-bit clocked D-type register with straight-across pinout
  AS6C6264: 8k x 8 bit CMOS static RAM
  74HC32: Quad 2-input OR gate
  74HC00: Quad NAND. The original 74xx part.
