# Fritzing sketch D-P-memory (saved by Fritzing 0.9.6b)
breadboards: 2

parts:
  U1 = 74HC245 [package="DIP (Dual Inline) [THT]"]
  U2 = 74HC245 [package="DIP (Dual Inline) [THT]"]
  U3 = 74HC574 [package="DIP (Dual Inline) [THT]"]
  U4 = 74HC245 [package="DIP (Dual Inline) [THT]"]
  U5 = 74HC574 [package="DIP (Dual Inline) [THT]"]
  U6 = 74HC245 [package="DIP (Dual Inline) [THT]"]
  U7 = AS6C6264 [package="DIP (Dual Inline) [THT]"]
  U8 = 74HC32 [package="DIP (Dual Inline) [THT]"]
  U9 = 74HC00 [package="DIP (Dual Inline) [THT]"]

nets:
  GND: U1.DIR, U1.GND, U2./DIR, U8.1A, U8.1B, U8.2A, U8.2B, U8.GND, U9.2A, U9.2B, U9.GND
  N1: U1.A1, U1.A8
  N2: U1.B8, U1.B1
  N3: U1.B5, U4.A5
  GND_2: U1./DIR, U3./OE, U3.GND, U4.GND, U5./OE, U5.GND, U6.GND, U8.3A, U8.3B
  VCC: U1.Vcc, U6.DIR, U8.Vcc
  N4: U2.DIR, U2.GND
  N5: U2.A1, U2.A8
  N6: U2.B8, U2.B1
  N7: U2.B5, U6.A5
  VCC_2: U2.Vcc, U3.Vcc, U4.Vcc, U5.Vcc, U6.Vcc, U7.Vss
  N8: U3.D0, U3.D7
  N9: U3.D4, U4.A4
  N10: U3.CLK, U5.CLK, U8.4Y
  N11: U3.Q7, U3.Q0
  N12: U3.Q4, U7.A4
  N13: U4.A1, U4.A8
  N14: U4.B8, U4.B1
  N15: U4.B6, U7.DQ5
  N16: U4.B2, U7.DQ1
  N17: U5.D0, U5.D7
  N18: U5.D4, U6.A4
  N19: U5.Q5, U7.A12
  N20: U5.Q4, U5.Q0
  N21: U5.Q2, U7.A11
  N22: U6.A1, U6.A8
  N23: U6.B5, U7./OE, U9.3A, U9.3B
  N24: U7.A7, U7.A0
  N25: U7.DQ0, U7.DQ2
  N26: U7.DQ3, U7.DQ7
  N27: U7.A10, U7.A8
  VCC_3: U7.CE2, U7.Vcc, U9.4A, U9.4B, U9.Vcc
  N28: U7./WE, U9.3Y

notes:
  Sysbus7:0 display driver, not a part of D/P subsystem.
  Gray wires are /opsels for D and P memory (from 138s).
  sysclk from clock module
  op/ctl from clock module
  574s are clocked on every ctl cycle. But we only enable the RAN when /opsel for D or P.
  op cycle 15:8 transceiver
  ctl/op from clock module
  ctl cycle 15:8 register
  op cycle 7:0 transceiver
  ctl cycle 7:0 register
  Control signals:
  NOTE: OP-PD# = (OPSEL-P# | OPSEL-D#). D or P unit selected, op-cycle.
  Display driver 245s: both DIR:1 and /OE strapped low.
  Op-cycle 15:8 transceiver: DIR:1 strapped inbound (high). /OE = CTL/OP
  Ctl-cycle 15:8 register: CLK = OP/CTL | SYSCLK. /OE:19 strapped low.
  Op-cycle 7:0 transceiver: DIR:1 = ! SYSBUS:12. /OE = (OP-PD#) | SYSCLK
  Ctl-cycle 7:0 register CLK = OP/CTL | SYSCLK. /OE strapped low.
  RAM /WE: SYSCLK | (OP-PD# | SYSBUS:12)
  RAM /OE: SYSCLK | (OP-PD# | ! SYSBUS:12)
  RAM /CE: OP-PD# (Or does this come to late for a chip enable? Could use CTL/OP.)
  RAM CE2: Strapped high.
  OP-PD# is OPSEL-P# AND OPSEL-D#. With a 7400, this is two gate delays. The inputs are SELs so they come about 50+ ns after clock. So this is valid during the second half of the cycle at 8MHz. Two NANDs.
  (OP/CTL | SYSCLK) and (OP-PD# | SYSCLK). Two ORs.
  One NAND for ! SYSBUS:12. Two ORs for OP-PD# SYSBUS:12 both polarities. Two more ORs for SYSCLK.
  So need TWO 7432s and one 7400.
  Maybe move the sysbus7:0 display driver below the 15:8 driver and move the 7400 to NE corner with the OR gates. More all the parts north and leave the free space at south. Can add an MITM part, like the 0s register for sysbus11:4, at south, then pass the sysbus westward into the MITM where it makes another exterious loop around the MITM's internal bus (which will also be wired in blue).

custom parts:
  74HC245: 8-bit bidrectional transceiver with straight-across pinout
  74HC574: 8-bit clocked D-type register with straight-across pinout
  AS6C6264: 8k x 8 bit CMOS static RAM
  74HC32: Quad 2-input OR gate
  74HC00: Quad NAND. The original 74xx part.
