# Fritzing sketch Flags (saved by Fritzing 0.9.6b)
breadboards: 2

parts:
  7486 = 74HC86 [package="DIP (Dual Inline) [THT]"]
  7421 = 74HC21 [package="DIP (Dual Inline) [THT]"]
  74HC2 = 74HC153 [package="DIP (Dual Inline) [THT]"]
  U2 = 74HC139 [package="DIP (Dual Inline) [THT]"]
  U1 = 74HC32 [package="DIP (Dual Inline) [THT]"]
  U3 = 74HC00 [package="DIP (Dual Inline) [THT]"]

nets:
  GND: 7486.1A, 7486.1B, 7486.2A, 7486.2B, 7486.GND, U2.1E#, U2.1A0, U2.1A1, U2.GND
  N1: 7486.3Y, U2.2A0
  N2: 7486.3B, U1.2Y
  N3: 7486.4Y, 7421.2A, 7421.2B, 74HC2.1I2
  N4: 7486.4A, 74HC2.2I2
  N5: 7486.4B, 74HC2.2I3
  VCC: 7486.Vcc, 74HC2.1I0, U2.VCC, U1.1A, U1.1B
  N6: 7421.1A, 7421.1B, U2.2Y0#
  N7: 7421.1C, U2.2Y1#
  N8: 7421.1D, U2.2Y3#
  GND_2: 7421.GND, 74HC2.GND, U1.GND, U3.1A, U3.1B, U3.2A, U3.2B, U3.GND
  N9: 7421.2Y, 74HC2.1I3
  N10: 7421.2C, 7421.2D, 74HC2.2I1, U1.3B
  VCC_2: 7421.Vcc, 74HC2.Vcc, U1.4A, U1.4B, U1.Vcc, U3.4A, U3.4B, U3.Vcc
  N11: 74HC2.1E#, U3.3Y
  N12: 74HC2.1I1, U1.3Y
  N13: 74HC2.1Y, U1.2A
  N14: 74HC2.2Y, U1.2B
  N15: 74HC2.2I0, U1.3A
  N16: 74HC2.2E#, U3.3A, U3.3B

notes:
  IR:2 REG_C IR:0 (org) dst_wr_en#
  IR:3 REG_Z (brn)
  RSW:2 REG_N (gry)
  IR:1 (pur) REG_V (grn)

custom parts:
  74HC86: Quad 2-input XOR gate with the usual pinout.
  74HC21: Dual 4-input AND gate
  74HC153: Dual 4-input mux
  74HC139: Dual 2-to-4 decoders with active low enable
  74HC32: Quad 2-input OR gate
  74HC00: Quad NAND. The original 74xx part.
