# Fritzing sketch RAM-16-busses (saved by Fritzing 0.9.6b)
circuit board: 8.46667cm x 5.64444cm
breadboards: 4

parts:
  U3 = 74HC245 [package="DIP (Dual Inline) [THT]"]
  U4 = 74HC245 [package="DIP (Dual Inline) [THT]"]
  U7 = 74HC20 [package="DIP (Dual Inline) [THT]"]
  U8 = 74HC00 [package="DIP (Dual Inline) [THT]"]
  U9 = 74HC08 [package="DIP (Dual Inline) [THT]"]
  U10 = 74HC139 [package="DIP (Dual Inline) [THT]"]
  U11 = AS6C6264 [package="DIP (Dual Inline) [THT]"]
  U12 = AS6C6264 [package="DIP (Dual Inline) [THT]"]
  U13 = AS6C6264 [package="DIP (Dual Inline) [THT]"]
  U14 = AS6C6264 [package="DIP (Dual Inline) [THT]"]
  U17 = 74HC245 [package="DIP (Dual Inline) [THT]"]
  U18 = 74HC157 [package="DIP (Dual Inline) [THT]"]
  U19 = 74HC32 [package="DIP (Dual Inline) [THT]"]
  U20 = DIP - 16 pins [chip_label=82ohm package="DIP (Dual Inline) [THT]"]
  U21 = DIP - 16 pins [chip_label=82ohm package="DIP (Dual Inline) [THT]"]
  U22 = DIP - 16 pins [chip_label=82ohm package="DIP (Dual Inline) [THT]"]
  U23 = DIP - 16 pins [chip_label=82ohm package="DIP (Dual Inline) [THT]"]

nets:
  N1: U3.A1, U3.A8
  N2: U3.A4, U4.A5
  N3: U3.A5, U11.DQ3
  GND: U3.GND, U4.GND, U13.A0, U13.Vss, U14.A0, U17.GND
  N4: U3.B8, U3.B1
  N5: U3.B4, U22.pin13
  VCC: U3.Vcc, U4.Vcc, U17.Vcc
  N6: U4.A1, U4.A8
  N7: U4.B8, U4.B1
  N8: U4.B4, U17.B5
  N9: U7.1A, U7.1D
  N10: U7.NC#2, U20.pin14
  N11: U7.2A, U7.2D
  N12: U7.NC#10, U20.pin7
  GND_2: U8.GND, U9.GND, U10.1E#, U10.GND, U18.GND
  VCC_2: U8.Vcc, U9.Vcc, U10.VCC, U11.DQ7, U11.Vcc, U12.Vcc, U18.VCC
  N13: U9.4A, U9.4B, U18.E#, U19.GND
  N14: U11.A12, U11.A1
  N15: U11.A4, U12.A4
  N16: U11.A0, U12.A0
  VSS: U11.Vss, U12.Vss
  N17: U11.DQ4, U12.DQ3
  N18: U11./CE, U11.A8
  N19: U11./OE, U14.A11
  N20: U11.A11, U12.A11
  N21: U12.A12, U12.A1
  N22: U12.A5, U13.A4
  N23: U13.A12, U13.A1
  N24: U13.A5, U14.A4
  N25: U13.DQ3, U17.A4
  N26: U13.DQ4, U14.DQ3
  VCC_3: U13.DQ7, U13.Vcc, U14.Vcc
  N27: U13./CE, U13.A8
  N28: U13./OE, U20.pin4
  N29: U13.A11, U14./OE
  N30: U14.A12, U14.A1
  N31: U14.A5, U21.pin5
  N32: U17.A1, U17.A8
  N33: U17.B8, U17.B1
  N34: U17.B4, U23.pin12
  N35: U20.pin1, U21.pin8
  N36: U20.pin6, U21.pin1
  N37: U20.pin12, U20.pin15
  N38: U20.pin16, U21.pin9
  N39: U22.pin1, U23.pin8
  N40: U22.pin16, U23.pin9

notes:
  Mem LB
  Sys LB
  Mem HB
  Sys LB
  Mem HB
  Sys HB
  HRLB
  LRLB
  HRHB
  LRHB
  Notes:
  HB, LB = High Byte, Low Byte
  Even bytes are low.
  HR, LR = High Range, Low Range. Byte addresses less than 16k are low range.
  Low byte RAM have A0 connected to ground. High byte RAMs have A0 connected to power.
  Transceivers connect memory bus LB to system bus LB ("Mem LB Sys LB"), or memory bus HB to system bus LB (for byte reads of odd addresses) or memory bus HB to system bus HB for the upper half of 16 bit reads.
  Wire colors:
  White - external data7:0
  Gray - external data15:8
  Green - address15:8
  Cyan - address7:0
  Blue - internal data (all - they don't cross.)
  In reality external busses are green and internal are blue.
  Note: "upper" and "lower" address wiring is a lie - A12 is located with A7:0 on the part, no help for it.

custom parts:
  74HC245: 8-bit bidrectional transceiver with straight-across pinout
  74HC20: Dual 4-input NAND gate
  74HC00: Quad NAND. The original 74xx part.
  74HC08: Quad positive AND gate
  74HC139: Dual 2-to-4 decoders with active low enable
  AS6C6264: 8k x 8 bit CMOS static RAM
  74HC157: Quad 2:1 mux
  74HC32: Quad 2-input OR gate
  DIP - 16 pins: A DIP stand-in part for whatever IC you want. With 16 pins on a 300mil dual inline package (DIP) footprint.
