# Fritzing sketch RAM-16 (saved by Fritzing 0.9.6b)
circuit board: 8.46667cm x 5.64444cm
breadboards: 4

parts:
  U3 = 74HC245 [package="DIP (Dual Inline) [THT]"]
  U4 = 74HC245 [package="DIP (Dual Inline) [THT]"]
  U7 = 74HC20 [package="DIP (Dual Inline) [THT]"]
  U8 = 74HC00 [package="DIP (Dual Inline) [THT]"]
  U9 = 74HC08 [package="DIP (Dual Inline) [THT]"]
  U10 = 74HC139 [package="DIP (Dual Inline) [THT]"]
  U11 = AS6C6264 [package="DIP (Dual Inline) [THT]"]
  U12 = AS6C6264 [package="DIP (Dual Inline) [THT]"]
  U13 = AS6C6264 [package="DIP (Dual Inline) [THT]"]
  U14 = AS6C6264 [package="DIP (Dual Inline) [THT]"]
  U17 = 74HC245 [package="DIP (Dual Inline) [THT]"]
  U18 = 74HC157 [package="DIP (Dual Inline) [THT]"]
  U23 = 74HC32 [package="DIP (Dual Inline) [THT]"]
  U20 = DIP - 16 pins [chip_label=82ohm package="DIP (Dual Inline) [THT]"]
  U21 = DIP - 16 pins [chip_label=82ohm package="DIP (Dual Inline) [THT]"]
  U22 = DIP - 16 pins [chip_label=82ohm package="DIP (Dual Inline) [THT]"]
  U23_2 = DIP - 16 pins [chip_label=82ohm package="DIP (Dual Inline) [THT]"]
  U100 = 74HC32 [package="DIP (Dual Inline) [THT]"]
  U101 = 74HC157 [package="DIP (Dual Inline) [THT]"]

nets:
  N1: U3.DIR, U4.DIR, U8.4A, U8.4B, U10.1A0, U10.2A1, U17.DIR, U18.1in0, U18.2in0, U20.pin1, U21.pin8
  N2: U3.A1, U3.A8
  GND: U3.GND, U4.GND, U13.A0, U13.Vss, U14.A0, U17.GND
  N3: U3.B8, U3.B1
  N4: U3./DIR, U17./DIR, U23.3Y
  VCC: U3.Vcc, U4.Vcc, U17.Vcc
  N5: U4.A1, U4.A8
  N6: U4.B8, U4.B1
  N7: U4./DIR, U23.4Y
  N8: U7.1A, U7.1D
  N9: U7.NC#2, U20.pin14
  N10: U7.1Y, U8.1B, U8.2B, U10.1A1, U11.CE2, U12.CE2, U13.CE2, U14.CE2
  N11: U7.2Y, U21.pin14
  N12: U7.2A, U7.2D
  N13: U7.NC#10, U20.pin7
  N14: U8.1A, U9.3Y
  N15: U8.1Y, U100.4A
  N16: U8.2A, U8.3Y
  N17: U8.2Y, U100.3A
  GND_2: U8.GND, U9.1A, U9.1B, U9.2A, U9.2B, U9.GND, U10.1E#, U10.GND, U18.GND
  N18: U8.3A, U9.3B, U11.A0, U12.A0, U18.S
  N19: U8.3B, U9.3A, U10.2A0, U20.pin2
  N20: U8.4Y, U18.3in0, U18.4in0
  VCC_2: U8.Vcc, U9.4Y, U9.4A, U9.Vcc, U10.VCC, U11.DQ0, U11.DQ7, U11.Vcc, U12.Vcc, U18.VCC, U100.Vcc
  N21: U10.1Y2#, U23.2A
  N22: U10.1Y3#, U23.1B
  N23: U10.2Y3#, U18.4in1
  N24: U10.2Y2#, U18.3in1
  N25: U10.2Y1#, U18.2in1
  N26: U10.2Y0#, U18.1in1
  N27: U11.A12, U11.A1
  VSS: U11.Vss, U12.Vss, U100.GND
  N28: U11./CE, U11.A8, U18.4Y#
  N29: U11./OE, U12./OE, U13./OE, U14./OE, U23.1Y
  N30: U11./WE, U12./WE, U13./WE, U14./WE, U23.2Y
  N31: U12.A12, U12.A1
  N32: U12.DQ0, U12.A8
  N33: U12./CE, U18.2Y#
  N34: U13.A12, U13.A1
  VCC_3: U13.DQ0, U13.DQ7, U13.Vcc, U14.Vcc
  N35: U13./CE, U13.A8, U18.1Y#
  N36: U14.A12, U14.A1
  N37: U14.DQ0, U14.A8
  N38: U14./CE, U18.3Y#
  N39: U17.A1, U17.A8
  N40: U17.B8, U17.B1
  GND_3: U18.E#, U23.GND, U101.2in0, U101.2in1, U101.GND, U101.4in1, U101.E#
  N41: U23.1A, U23.2B, U23.3A, U23.4A, U100.1A, U100.2B
  N42: U23.3B, U100.3Y
  N43: U23.4B, U100.4Y
  VCC_4: U23.Vcc, U101.4in0, U101.VCC
  N44: U20.pin6, U21.pin1
  N45: U20.pin12, U20.pin15, U20.pin16, U21.pin9
  N46: U22.pin1, U23_2.pin8
  N47: U22.pin16, U23_2.pin9
  N48: U100.2A, U101.1Y#
  N49: U100.3B, U100.4B

notes:
  Mem LB
  Sys LB
  Mem HB
  Sys LB
  Mem HB
  Sys HB
  HRLB
  LRLB
  HRHB
  LRHB
  Notes:
  HB, LB = High Byte, Low Byte
  Even bytes are low.
  HR, LR = High Range, Low Range. Byte addresses less than 16k are low range.
  Low byte RAM have A0 connected to ground. High byte RAMs have A0 connected to power.
  Transceivers connect memory bus LB to system bus LB ("Mem LB Sys LB"), or memory bus HB to system bus LB (for byte reads of odd addresses) or memory bus HB to system bus HB for the upper half of 16 bit reads.
  The white net is the RAM/IO# signal. It originates at the 7420 upper right. Orange is M16#.
  The 7432 at upper left (U96) is a kludge, a fix for a mistake - the original design just enabled the memory on the bus for *every* cycle, like nothing else could ever drive the bus. ;-) Now the gray line has to be low; it's MEM_EN#. Else the transceivers are not enabled (dark brown wires to pin 19 of the 3 transceivers).
  MEM_EN# comes from the SYSDATA_SRC decoder in Central which decodes the K reg. This comment applies to the "C" and "D" gates on the right side of the chip as viewed.
  The A unit of U100 mixes the read signal for the IR with sysclk. This is also on the Kludge page in KiCad. The gray wire on pin 2 is IR read from the microcode.
  The B unit mixes the clock signal for the IR with sysclk. The unclocked signal comes from either microcode or the Nano as determined by the mux U101, which selects on YARC/NANO# from the northmost pin on the 6-pin connector with the green bus attached. The bus lines come from the Nano's decoders and MCR.
  The C unit of the mux U101 is the write enable to the YARC's registers. The Nano can enable and disable it. The D unit looks unused, but it actually drives the address transceiver enable to YARC. Currently it just inverts YARC/NANO#. A planned enhancement may make this more complex in the future.
  IR read mem_read ir_wr address xcvr en Blue bus to YARC
  from ucode six-pin from ucode ucode to central Green bus is from MCR and Nano's decoders I/O decoder
  |---------------| these three lines are the register write enable to U93B in the register control logic

custom parts:
  74HC245: 8-bit bidrectional transceiver with straight-across pinout
  74HC20: Dual 4-input NAND gate
  74HC00: Quad NAND. The original 74xx part.
  74HC08: Quad positive AND gate
  74HC139: Dual 2-to-4 decoders with active low enable
  AS6C6264: 8k x 8 bit CMOS static RAM
  74HC157: Quad 2:1 mux
  74HC32: Quad 2-input OR gate
  DIP - 16 pins: A DIP stand-in part for whatever IC you want. With 16 pins on a 300mil dual inline package (DIP) footprint.
