# Fritzing sketch Registers (saved by Fritzing 0.9.6b)
breadboards: 6

parts:
  U1 = 74HC670 [package="DIP (Dual Inline) [THT]"]
  U2 = 74HC670 [package="DIP (Dual Inline) [THT]"]
  U3 = 74HC670 [package="DIP (Dual Inline) [THT]"]
  U4 = 74HC670 [package="DIP (Dual Inline) [THT]"]
  U5 = 74HC670 [package="DIP (Dual Inline) [THT]"]
  U6 = 74HC670 [package="DIP (Dual Inline) [THT]"]
  U7 = 74HC670 [package="DIP (Dual Inline) [THT]"]
  U8 = 74HC670 [package="DIP (Dual Inline) [THT]"]
  U9 = 74HC245 [package="DIP (Dual Inline) [THT]"]
  U10 = 74HC245 [package="DIP (Dual Inline) [THT]"]
  U11 = 74HC245 [package="DIP (Dual Inline) [THT]"]
  U12 = 74HC245 [package="DIP (Dual Inline) [THT]"]
  U13 = 74HC157 [package="DIP (Dual Inline) [THT]"]
  U14 = 74HC157 [package="DIP (Dual Inline) [THT]"]
  U15 = 74HC157 [package="DIP (Dual Inline) [THT]"]
  U16 = 74HC157 [package="DIP (Dual Inline) [THT]"]
  U17 = 74HC245 [package="DIP (Dual Inline) [THT]"]
  U19 = 74HC00 [package="DIP (Dual Inline) [THT]"]

nets:
  N1: U1.D1, U5.D2
  N2: U1.D3, U1.D0
  N3: U1.RA1, U2.RA1, U3.RA1, U4.RA1
  N4: U1.RA0, U2.RA0, U3.RA0, U4.RA0
  N5: U1.Q3, U1.Q1
  GND: U1.GND, U2.GND, U3.GND, U4.GND, U9.A2, U9.A7, U10.A2, U10.A7, U13.E#, U14.E#, U15.E#, U16.E#
  N6: U1.RE#, U2.RE#, U3.RE#, U4.RE#
  N7: U1.WE#, U1.WA0
  N8: U1.WA1, U2.WA1, U3.WA1, U4.WA1, U5.WA1, U6.WA1, U7.WA1, U8.WA1
  VCC: U1.Vcc, U2.Vcc, U3.Vcc, U4.Vcc
  N9: U2.D1, U7.D2
  N10: U2.D3, U2.D0
  N11: U2.Q3, U2.Q1
  N12: U2.WE#, U2.WA0
  N13: U3.D1, U8.D2
  N14: U3.D3, U3.D0
  N15: U3.Q3, U3.Q1
  N16: U3.WE#, U3.WA0
  N17: U4.D1, U6.D2
  N18: U4.D3, U4.D0
  N19: U4.Q3, U4.Q1
  N20: U4.WE#, U4.WA0
  N21: U5.D3, U5.D0
  N22: U5.RA1, U6.RA1, U7.RA1, U8.RA1
  N23: U5.RA0, U6.RA0, U7.RA0, U8.RA0
  N24: U5.Q3, U5.Q0
  GND_2: U5.GND, U6.GND, U7.GND, U8.GND, U11.A3, U11.A6, U12.A3, U12.A6
  GND_3: U5.RE#, U6.RE#, U7.RE#, U8.RE#, U11.GND, U12.GND
  N25: U5.WE#, U5.WA0
  N26: U6.D3, U6.D0
  N27: U6.Q3, U6.Q1
  N28: U6.WE#, U6.WA0
  VCC_2: U6.Vcc, U7.Vcc, U8.Vcc
  N29: U7.D3, U7.D0
  N30: U7.Q3, U7.Q0
  N31: U7.WE#, U7.WA0
  N32: U8.D3, U8.D0
  N33: U8.Q3, U8.Q0
  N34: U8.WE#, U8.WA0
  N35: U9.DIR, U10.DIR
  N36: U9.A1, U9.A8
  GND_4: U9.GND, U10.GND, U17.DIR, U17.GND, U19.GND
  N37: U9./DIR, U10./DIR
  VCC_3: U9.Vcc, U10.Vcc, U17.Vcc, U19.Vcc
  N38: U10.A1, U10.A8
  N39: U11.A1, U11.A8
  VCC_4: U11.Vcc, U12.Vcc
  N40: U12.A1, U12.A8
  N41: U13.S, U14.S, U15.S, U16.S
  GND_5: U13.GND, U14.GND, U15.GND, U16.GND
  VCC_5: U13.VCC, U14.VCC, U15.VCC, U16.VCC
  N42: U17.B8, U17.B7, U17.B6, U17.B5, U17.B4, U17.B3, U17.B2, U17.B1

custom parts:
  74HC670: 4x4 bit register file
  74HC245: 8-bit bidrectional transceiver with straight-across pinout
  74HC157: Quad 2:1 mux
  74HC00: Quad NAND. The original 74xx part.
