# Fritzing sketch microcode (saved by Fritzing 0.9.6b)
breadboards: 6

parts:
  U1 = 74HC245 [package="DIP (Dual Inline) [THT]"]
  U2 = 74HC245 [package="DIP (Dual Inline) [THT]"]
  U3 = AS6C6264 [package="DIP (Dual Inline) [THT]"]
  U4 = AS6C6264 [package="DIP (Dual Inline) [THT]"]
  U5 = AS6C6264 [package="DIP (Dual Inline) [THT]"]
  U10 = AS6C6264 [package="DIP (Dual Inline) [THT]"]
  U11 = 74HC245 [package="DIP (Dual Inline) [THT]"]
  U12 = 74HC245 [package="DIP (Dual Inline) [THT]"]
  U13 = 74HC245 [package="DIP (Dual Inline) [THT]"]
  U14 = 74HC245 [package="DIP (Dual Inline) [THT]"]
  U15 = 74HC193 [package="DIP (Dual Inline) [THT]"]
  U16 = 74HC193 [package="DIP (Dual Inline) [THT]"]
  U17 = 74HC574 [package="DIP (Dual Inline) [THT]"]
  U18 = 74HC574 [package="DIP (Dual Inline) [THT]"]
  U20 = 74HC157 [package="DIP (Dual Inline) [THT]"]
  U21 = 74HC157 [package="DIP (Dual Inline) [THT]"]
  U22 = 74HC574 [package="DIP (Dual Inline) [THT]"]
  U23 = 74HC139 [package="DIP (Dual Inline) [THT]"]
  U24 = 74HC32 [package="DIP (Dual Inline) [THT]"]
  U25 = 74HC32 [package="DIP (Dual Inline) [THT]"]
  U26 = 74HC157 [package="DIP (Dual Inline) [THT]"]
  U28 = 74HC574 [package="DIP (Dual Inline) [THT]"]
  U29 = 74HC574 [package="DIP (Dual Inline) [THT]"]
  U30 = 74HC574 [package="DIP (Dual Inline) [THT]"]
  U31 = 74HC574 [package="DIP (Dual Inline) [THT]"]

nets:
  N1: U1.A1, U1.A8
  N2: U1.A5, U31.D4
  N3: U1.B8, U1./DIR
  N4: U2.A1, U2.A8
  N5: U2.B8, U2./DIR
  N6: U3.A5, U3.A0
  N7: U4.A5, U4.A0
  N8: U4.DQ0, U4.DQ7
  N9: U4.DQ3, U12.B5
  N10: U4.DQ4, U12.A5
  N11: U5.A5, U5.A0
  N12: U5.A3, U16.UP
  N13: U5.A2, U10.A3
  N14: U5.Vss, U30./OE
  N15: U10.A5, U10.A0
  N16: U11.A1, U11.A8
  N17: U11.B8, U11./DIR
  N18: U11.B4, U28.D3
  N19: U12.A1, U12.A8
  N20: U12.A4, U28.D4
  GND: U12.GND, U28./OE, U28.GND
  N21: U12.B8, U12./DIR
  N22: U12.B4, U22.D4
  N23: U13.A1, U13.A8
  N24: U13.A4, U22.D3
  N25: U13.A5, U17.Q3
  GND_2: U13.GND, U14.GND, U22.GND, U26.E#
  N26: U13.B8, U13.B1
  N27: U13.B4, U17.D4
  VCC: U13.Vcc, U14.Vcc
  N28: U14.A1, U14.A8
  N29: U14.A5, U18.Q3
  N30: U14.B8, U14.B1
  N31: U14.B5, U18.D3
  N32: U15.QB, U15.QD
  N33: U16.QB, U16.QD
  N34: U17.D0, U17.D7
  GND_3: U17.GND, U18.GND
  N35: U17.Q7, U17.Q0
  VCC_2: U17.Vcc, U20.VCC, U21.VCC, U23.VCC, U26.VCC
  N36: U18.D0, U18.D7
  N37: U18.Q7, U18.Q0
  GND_4: U20.GND, U21.GND, U23.GND, U26.GND
  N38: U22.D0, U22.D7
  N39: U22.Q6, U23.2E#
  N40: U22.Q5, U23.2A1
  N41: U22.Q4, U23.2A0
  N42: U22.Q2, U23.1E#
  N43: U22.Q1, U23.1A1
  N44: U22.Q0, U23.1A0
  N45: U23.1Y0#, U23.1Y3#
  N46: U23.2Y3#, U26.4in0
  N47: U23.2Y2#, U26.3in0
  N48: U23.2Y1#, U26.2in0
  N49: U23.2Y0#, U26.1in0
  N50: U24.1A, U24.2A, U24.3B, U24.4B, U25.1A, U25.2A, U25.3B, U25.4B, U26.1in1, U26.2in1, U26.3in1, U26.4in1
  N51: U26.1Y#, U28.CLK
  N52: U26.2Y#, U29.CLK
  N53: U26.3Y#, U30.CLK
  N54: U26.4Y#, U31.CLK
  N55: U28.D0, U28.D7
  N56: U28.Q7, U28.Q0
  N57: U29.D0, U29.D7
  N58: U29.Q7, U29.Q0
  N59: U30.D0, U30.D7
  N60: U30.Q7, U30.Q0
  N61: U31.D0, U31.D7
  N62: U31.Q7, U31.Q0

custom parts:
  74HC245: 8-bit bidrectional transceiver with straight-across pinout
  AS6C6264: 8k x 8 bit CMOS static RAM
  74HC193: 4-bit synchronous up/down counter with parallel load
  74HC574: 8-bit clocked D-type register with straight-across pinout
  74HC157: Quad 2:1 mux
  74HC139: Dual 2-to-4 decoders with active low enable
  74HC32: Quad 2-input OR gate
